// Logisim project scheme.circ as structural Verilog
module Arithmetic_Logic_Unit (
  input  EF,
  input  EZ,
  input  [7:0] O,
  input  [7:0] D,
  input  LX,
  input  C,
  input  LY,
  input  R,
  input  i,
  output [7:0] D_2
);

  wire Adc___Sbb_o, and_1_out, and_2_out, and_3_out, and_4_out, and_5_out, and_6_out, and_7_out, or_1_out,
       or_2_out, Right_Shift_p4;
  wire [3:0] or_3_out;
  wire [7:0] Adc___Sbb_s, Bitwise_AND_p3, Bitwise_NOR_p3, Bitwise_OR_p3, Decoder_d, multiplexor_1_s, Reg_X_q,
       Reg_Y_q, Right_Shift_p3;

  Multiplexor multiplexor_1 (.A({8{1'b0}}), .B(O), .S(multiplexor_1_s), .M(O[7]));
  and and_1 (and_1_out, C, LX);
  and and_2 (and_2_out, C, LY);
  and and_3 (and_3_out, multiplexor_1_s[4], multiplexor_1_s[6]);
  Decoder Decoder (.C(multiplexor_1_s[6:4]), .E(EZ), .D(Decoder_d));
  D_Latch Reg_X (.D(D), .R(R), .E(and_1_out), .Q(Reg_X_q));
  D_Latch Reg_Y (.D(D), .R(R), .E(and_2_out), .Q(Reg_Y_q));
  and and_4 (and_4_out, and_3_out, ~multiplexor_1_s[5]);  // AND_Gate
  and and_5 (and_5_out, multiplexor_1_s[5], multiplexor_1_s[6]);
  // Probe on Reg_X_q
  // Probe on Reg_Y_q
  // BitAnd Bitwise_AND: pin names not known; wires that end beside it: Reg_X_q, Reg_Y_q, Bitwise_AND_p3
  // BitOr Bitwise_OR: pin names not known; wires that end beside it: Reg_X_q, Reg_Y_q, Bitwise_OR_p3
  // BitNor Bitwise_NOR: pin names not known; wires that end beside it: Reg_X_q, Reg_Y_q, Bitwise_NOR_p3
  // RightShift Right_Shift: pin names not known; wires that end beside it: Reg_X_q, i, Right_Shift_p3, Right_Shift_p4
  AdcSbb Adc___Sbb (.M(Decoder_d[7]), .i(i), .A(Reg_X_q), .B(Reg_Y_q), .S(Adc___Sbb_s), .o(Adc___Sbb_o));
  and and_6 (and_6_out, Right_Shift_p4, and_4_out);
  and and_7 (and_7_out, Adc___Sbb_o, and_5_out);
  Comparator Comparator (.A(Reg_X_q), .B(Reg_Y_q), .A_B(or_3_out[1]), .A_B_2(or_3_out[2]), .A_B_3(or_3_out[3]));
  or or_1 (or_1_out, EF, Decoder_d[1]);
  assign D_2 = Decoder_d[0] ? Reg_X_q : 8'bz;  // Controlled_Buffer controlled_buffer_1
  assign D_2 = Decoder_d[2] ? Bitwise_AND_p3 : 8'bz;  // Controlled_Buffer controlled_buffer_2
  assign D_2 = Decoder_d[3] ? Bitwise_OR_p3 : 8'bz;  // Controlled_Buffer controlled_buffer_3
  assign D_2 = Decoder_d[4] ? Bitwise_NOR_p3 : 8'bz;  // Controlled_Buffer controlled_buffer_4
  assign D_2 = Decoder_d[5] ? Right_Shift_p3 : 8'bz;  // Controlled_Buffer controlled_buffer_5
  or or_2 (or_2_out, Decoder_d[6], Decoder_d[7]);
  assign D_2 = or_2_out ? Adc___Sbb_s : 8'bz;  // Controlled_Buffer controlled_buffer_6
  or or_3 (or_3_out[0], and_6_out, and_7_out);
  assign D_2 = or_1_out ? {4'b0000, or_3_out} : 8'bz;  // Controlled_Buffer controlled_buffer_7

  // Notes on the sheet:
  //   Arithmetic Logic Unit
endmodule

module General_Purpose_Registers (
  input  LF,
  input  LG,
  input  [7:0] D,
  input  LH,
  input  R,
  input  [7:0] O,
  input  C,
  input  LR,
  input  ER,
  input  AR,
  output [7:0] D_2,
  output i,
  output [15:0] A
);

  wire and_1_out, and_2_out, and_3_out, and_4_out, or_1_out, or_2_out, or_3_out;
  wire [7:0] Input_d, Output_d, Reg_A_q, Reg_B_q, Reg_C_q, Reg_D_q, Reg_E_q, Reg_G_q, Reg_H_q;
  wire [7:1] Reg_F_q;

  Decoder Input (.C(O[2:0]), .E(and_1_out), .D(Input_d));
  and and_1 (and_1_out, C, LR);
  Decoder Output (.C(O[2:0]), .E(ER), .D(Output_d));
  D_Latch Reg_A (.D(D), .R(R), .E(Input_d[0]), .Q(Reg_A_q));
  assign D_2 = Output_d[0] ? Reg_A_q : 8'bz;  // Controlled_Buffer controlled_buffer_1
  D_Latch Reg_B (.D(D), .R(R), .E(Input_d[1]), .Q(Reg_B_q));
  assign D_2 = Output_d[1] ? Reg_B_q : 8'bz;  // Controlled_Buffer controlled_buffer_2
  assign D_2 = Output_d[2] ? Reg_C_q : 8'bz;  // Controlled_Buffer controlled_buffer_3
  D_Latch Reg_C (.D(D), .R(R), .E(Input_d[2]), .Q(Reg_C_q));
  assign D_2 = Output_d[3] ? Reg_D_q : 8'bz;  // Controlled_Buffer controlled_buffer_4
  D_Latch Reg_D (.D(D), .R(R), .E(Input_d[3]), .Q(Reg_D_q));
  and and_2 (and_2_out, C, LF);
  and and_3 (and_3_out, C, LG);
  and and_4 (and_4_out, C, LH);
  or or_1 (or_1_out, and_2_out, Input_d[5]);
  or or_2 (or_2_out, and_3_out, Input_d[6]);
  or or_3 (or_3_out, and_4_out, Input_d[7]);
  D_Latch Reg_E (.D(D), .R(R), .E(Input_d[4]), .Q(Reg_E_q));
  D_Latch Reg_F (.D(D), .R(R), .E(or_1_out), .Q({Reg_F_q, i}));
  D_Latch Reg_G (.D(D), .R(R), .E(or_2_out), .Q(Reg_G_q));
  D_Latch Reg_H (.D(D), .R(R), .E(or_3_out), .Q(Reg_H_q));
  assign D_2 = Output_d[4] ? Reg_E_q : 8'bz;  // Controlled_Buffer controlled_buffer_5
  assign D_2 = Output_d[5] ? {Reg_F_q, i} : 8'bz;  // Controlled_Buffer controlled_buffer_6
  assign D_2 = Output_d[6] ? Reg_G_q : 8'bz;  // Controlled_Buffer controlled_buffer_7
  assign D_2 = Output_d[7] ? Reg_H_q : 8'bz;  // Controlled_Buffer controlled_buffer_8
  assign A = AR ? {Reg_H_q, Reg_G_q} : 16'bz;  // Controlled_Buffer controlled_buffer_9
endmodule

module Program_Counter (
  input  LC,
  input  S,
  input  RC,
  input  C,
  input  R,
  input  IC,
  input  [7:0] D,
  input  EC,
  input  AC,
  input  [15:0] A,
  output [7:0] D_2,
  output [15:0] A_2,
  output COF
);

  wire and_1_out, and_2_out, Increment_o, nor_1_out, nor_2_out;
  wire [7:0] Addr___Data_2_s, Addr___Data_s, High_byte_q, Increment_2_s, Increment_s, Low___High_s,
       Low_byte_q, New___Last_2_s, New___Last_s;

  Multiplexor Addr___Data (.A(A[7:0]), .B(D), .S(Addr___Data_s), .M(and_1_out));
  and and_1 (and_1_out, ~S, LC);  // AND_Gate
  and and_2 (and_2_out, S, LC);
  Multiplexor Addr___Data_2 (.A(A[15:8]), .B(D), .S(Addr___Data_2_s), .M(and_2_out));
  nor nor_1 (nor_1_out, and_1_out, RC);
  Multiplexor New___Last (.A(Addr___Data_s), .B(Increment_s), .S(New___Last_s), .M(nor_1_out));
  nor nor_2 (nor_2_out, RC, and_2_out);
  Multiplexor New___Last_2 (.A(Addr___Data_2_s), .B(Increment_2_s), .S(New___Last_2_s), .M(nor_2_out));
  D_FlipFlop Low_byte (.D(New___Last_s), .R(R), .C(C), .Q(Low_byte_q));
  D_FlipFlop High_byte (.D(New___Last_2_s), .R(R), .C(C), .Q(High_byte_q));
  HalfAdder Increment (.i(IC), .A(Low_byte_q), .o(Increment_o), .S(Increment_s));
  HalfAdder Increment_2 (.i(Increment_o), .A(High_byte_q), .o(COF), .S(Increment_2_s));
  // Probe on Increment_s
  Multiplexor Low___High (.A(Low_byte_q), .B(High_byte_q), .S(Low___High_s), .M(S));
  // Probe on Increment_2_s
  assign D_2 = EC ? Low___High_s : 8'bz;  // Controlled_Buffer controlled_buffer_1
  assign A_2 = AC ? {High_byte_q, Low_byte_q} : 16'bz;  // Controlled_Buffer controlled_buffer_2

  // Notes on the sheet:
  //   Program Counter
endmodule

module Stack_Pointer (
  input  DS,
  input  IS,
  input  R,
  input  ES,
  input  AS,
  input  LS,
  input  S,
  input  [7:0] D,
  input  C,
  output [7:0] D_2,
  output [15:0] A,
  output SOF
);

  wire and_1_out, and_2_out, and_3_out, and_4_out, Inc___Dec_o, or_1_out;
  wire [7:0] High_byte_q, Inc___Dec_2_s, Inc___Dec_s, Input_2_s, Input_s, Low_byte_q, Output_s;

  Multiplexor Input (.A(Inc___Dec_s), .B(D), .S(Input_s), .M(and_1_out));
  and and_1 (and_1_out, ~S, LS);  // AND_Gate
  and and_2 (and_2_out, S, LS);
  Multiplexor Input_2 (.A(Inc___Dec_2_s), .B(D), .S(Input_2_s), .M(and_2_out));
  or or_1 (or_1_out, IS, DS);
  and and_3 (and_3_out, or_1_out, C);
  and and_4 (and_4_out, Inc___Dec_o, and_3_out);
  D_FlipFlop Low_byte (.D(Input_s), .R(R), .C(and_3_out), .Q(Low_byte_q));
  D_FlipFlop High_byte (.D(Input_2_s), .R(R), .C(and_4_out), .Q(High_byte_q));
  IncDec Inc___Dec (.M(DS), .o(Inc___Dec_o), .A(Low_byte_q), .S(Inc___Dec_s));
  IncDec Inc___Dec_2 (.M(DS), .o(SOF), .A(High_byte_q), .S(Inc___Dec_2_s));
  Multiplexor Output (.A(Low_byte_q), .B(High_byte_q), .S(Output_s), .M(S));
  assign D_2 = ES ? Output_s : 8'bz;  // Controlled_Buffer controlled_buffer_1
  assign A = AS ? {High_byte_q, Low_byte_q} : 16'bz;  // Controlled_Buffer controlled_buffer_2
endmodule

module Memory_Address_Register (
  input  LM,
  input  C,
  input  R,
  input  [15:0] A,
  output [15:0] A_2
);

  wire and_1_out;

  and and_1 (and_1_out, C, LM);
  D_Latch Low_byte (.D(A[7:0]), .R(R), .E(and_1_out), .Q(A_2[7:0]));
  D_Latch High_byte (.D(A[15:8]), .R(R), .E(and_1_out), .Q(A_2[15:8]));

  // Notes on the sheet:
  //   Memory Address Register
endmodule

module Instruction_Register (
  input  LI,
  input  C,
  input  R,
  input  [7:0] D,
  output [7:0] O
);

  wire and_1_out;

  and and_1 (and_1_out, C, LI);
  D_Latch Instruction (.D(D), .R(R), .E(and_1_out), .Q(O));

  // Notes on the sheet:
  //   Instruction Register
endmodule

module Step_Counter (
  input  HLT,
  input  CLK,
  input  INT,
  input  COF,
  input  SOF,
  input  XT,
  input  R,
  output C,
  output [2:0] T
);

  wire nand_1_out, nor_1_out, or_1_out, or_2_out;
  wire [7:0] Increment_s, Next___Reset_s;
  wire [7:3] Step_q;

  or or_1 (or_1_out, HLT, INT);
  or or_2 (or_2_out, COF, SOF);
  nor nor_1 (nor_1_out, or_1_out, or_2_out);
  nand nand_1 (nand_1_out, CLK, nor_1_out);
  Multiplexor Next___Reset (.A(Increment_s), .B({8{1'b0}}), .S(Next___Reset_s), .M(XT));
  not not_1 (C, nand_1_out);
  D_FlipFlop Step (.D(Next___Reset_s), .R(R), .C(nand_1_out), .Q({Step_q, T}));
  HalfAdder Increment (.i(1'b1), .A({Step_q, T}), .S(Increment_s));  // open: o

  // Notes on the sheet:
  //   Step Counter
endmodule
